// Logisim project Pipeline.circ as structural Verilog: 13 circuits, main circuit main
module main (
  input  WRITE_FLAG,
  input  [2:0] in_2,
  input  [15:0] in_3,
  input  [15:0] in_4,
  output [15:0] out_5
);

  wire [15:0] adder_1_out, and_1_out, not_1_out, or_1_out, shifter_1_out, shifter_2_out, subtractor_1_out,
       xor_1_out;

  Adder #(.width(16)) adder_1 (.a(in_3), .b(in_4), .out(adder_1_out));  // open: cin, cout
  Subtractor #(.width(16)) subtractor_1 (.a(in_3), .b(in_4), .out(subtractor_1_out));  // open: bin, bout
  assign or_1_out = in_3 | in_4;  // OR_Gate or_1, 16 bits wide
  assign and_1_out = in_3 & in_4;  // AND_Gate and_1, 16 bits wide
  assign not_1_out = ~in_4;  // NOT_Gate not_1, 16 bits wide
  assign xor_1_out = in_3 ^ in_4;  // XOR_Gate xor_1, 16 bits wide
  Shifter #(.width(16)) shifter_1 (.in(in_3), .\dist (in_4[3:0]), .out(shifter_1_out));
  Shifter #(.shift("lr"), .width(16)) shifter_2 (.in(in_3), .\dist (in_4[3:0]), .out(shifter_2_out));
  Multiplexer #(.select(3), .width(16)) multiplexer_1 (
    .in0(adder_1_out), .in1(subtractor_1_out), .in2(or_1_out), .in3(and_1_out), .in4(not_1_out),
    .in5(xor_1_out), .in6(shifter_1_out), .in7(shifter_2_out), .out(out_5), .sel(in_2));
endmodule

module RegisterFile (
  input  WRITE_EN,
  input  [2:0] RD,
  input  [2:0] RS,
  input  [15:0] WRITE_DATA,
  input  in_5,
  input  [2:0] REG_WRITE,
  output [15:0] A_OUT,
  output [15:0] B_OUT
);

  wire demultiplexer_1_out0, demultiplexer_1_out1, demultiplexer_1_out2, demultiplexer_1_out3,
       demultiplexer_1_out4, demultiplexer_1_out5, demultiplexer_1_out6, demultiplexer_1_out7;
  wire [15:0] register_1_q, register_2_q, register_3_q, register_4_q, register_5_q, register_6_q,
       register_7_q, register_8_q;

  Demultiplexer #(.select(3)) demultiplexer_1 (
    .out0(demultiplexer_1_out0), .out1(demultiplexer_1_out1), .out2(demultiplexer_1_out2),
    .out3(demultiplexer_1_out3), .out4(demultiplexer_1_out4), .out5(demultiplexer_1_out5),
    .out6(demultiplexer_1_out6), .out7(demultiplexer_1_out7), .in(WRITE_EN), .sel(REG_WRITE));
  Register #(.width(16)) register_1 (
    .D(WRITE_DATA), .en(demultiplexer_1_out0), .clk(in_5), .Q(register_1_q));  // open: clr
  Register #(.width(16)) register_2 (
    .D(WRITE_DATA), .en(demultiplexer_1_out1), .clk(in_5), .Q(register_2_q));  // open: clr
  Register #(.width(16)) register_3 (
    .D(WRITE_DATA), .en(demultiplexer_1_out2), .clk(in_5), .Q(register_3_q));  // open: clr
  Register #(.width(16)) register_4 (
    .D(WRITE_DATA), .en(demultiplexer_1_out3), .clk(in_5), .Q(register_4_q));  // open: clr
  Register #(.width(16)) register_5 (
    .D(WRITE_DATA), .en(demultiplexer_1_out4), .clk(in_5), .Q(register_5_q));  // open: clr
  Register #(.width(16)) register_6 (
    .D(WRITE_DATA), .en(demultiplexer_1_out5), .clk(in_5), .Q(register_6_q));  // open: clr
  Register #(.width(16)) register_7 (
    .D(WRITE_DATA), .en(demultiplexer_1_out6), .clk(in_5), .Q(register_7_q));  // open: clr
  Register #(.width(16)) register_8 (
    .D(WRITE_DATA), .en(demultiplexer_1_out7), .clk(in_5), .Q(register_8_q));  // open: clr
  Multiplexer #(.select(3), .width(16)) multiplexer_1 (
    .in0(register_1_q), .in1(register_2_q), .in2(register_3_q), .in3(register_4_q), .in4(register_5_q),
    .in5(register_6_q), .in6(register_7_q), .in7(register_8_q), .out(B_OUT), .sel(RS));
  Multiplexer #(.select(3), .width(16)) multiplexer_2 (
    .in0(register_1_q), .in1(register_2_q), .in2(register_3_q), .in3(register_4_q), .in4(register_5_q),
    .in5(register_6_q), .in6(register_7_q), .in7(register_8_q), .out(A_OUT), .sel(RD));
endmodule

module CPU (
);

  wire clock_1_out, clock_2_out, controller_1_jmp, controller_1_mem_write, controller_1_r_i,
       controller_1_reg_write, controller_1_sign_ext, is_zero_1_out_2, is_zero_2_out_2;
  wire [1:0] controller_1_jmp_mode, controller_1_written;
  wire [2:0] controller_1_alu_func, controller_1_reg_d, controller_1_reg_s;
  wire [7:0] controller_1_imm8;
  wire [15:0] adder_1_out, bit_extender_1_out, bit_extender_2_out, counter_1_q, main_1_out_5,
       multiplexer_1_out, multiplexer_2_out, multiplexer_3_out, multiplexer_4_out, multiplexer_5_out,
       multiplexer_6_out, multiplexer_7_out, multiplexer_8_out, ram_1_dout, registerfile_1_a_out,
       registerfile_1_b_out, rom_1_data;

  Adder #(.width(16)) adder_1 (.a(16'h1), .b(counter_1_q), .out(adder_1_out));  // open: cin, cout
  IS_ZERO is_zero_1 (.in_1(registerfile_1_a_out), .out_2(is_zero_1_out_2));
  Counter #(.max('hffff), .width(16)) counter_1 (
    .load(1'b1), .D(multiplexer_1_out), .Q(counter_1_q), .clk(clock_1_out));  // open: count, carry, up, clr
  Multiplexer #(.width(16)) multiplexer_1 (
    .in0(adder_1_out), .in1(multiplexer_2_out), .out(multiplexer_1_out), .sel(controller_1_jmp));
  Multiplexer #(.select(2), .width(16)) multiplexer_2 (
    .in0(multiplexer_6_out), .in1(multiplexer_3_out), .in2(multiplexer_4_out), .in3(counter_1_q),
    .out(multiplexer_2_out), .sel(controller_1_jmp_mode));
  ROM #(.addrWidth(16), .dataWidth(16)) rom_1 (.addr(counter_1_q), .data(rom_1_data));
  Multiplexer #(.width(16)) multiplexer_3 (
    .in0(adder_1_out), .in1(multiplexer_6_out), .out(multiplexer_3_out), .sel(is_zero_1_out_2));
  Multiplexer #(.width(16)) multiplexer_4 (
    .in0(multiplexer_6_out), .in1(adder_1_out), .out(multiplexer_4_out), .sel(is_zero_2_out_2));
  IS_ZERO is_zero_2 (.in_1(registerfile_1_a_out), .out_2(is_zero_2_out_2));
  Clock clock_1 (.out(clock_1_out));
  assign bit_extender_1_out = {{8{1'b0}}, controller_1_imm8};  // Bit_Extender bit_extender_1
  assign bit_extender_2_out = {{8{controller_1_imm8[7]}}, controller_1_imm8};  // Bit_Extender bit_extender_2
  RegisterFile registerfile_1 (
    .RS(controller_1_reg_s), .WRITE_DATA(multiplexer_8_out), .WRITE_EN(controller_1_reg_write),
    .in_5(clock_1_out), .RD(controller_1_reg_d), .A_OUT(registerfile_1_a_out), .B_OUT(registerfile_1_b_out));  // open: REG_WRITE
  Multiplexer #(.width(16)) multiplexer_5 (
    .in0(bit_extender_1_out), .in1(bit_extender_2_out), .out(multiplexer_5_out), .sel(controller_1_sign_ext));
  Multiplexer #(.width(16)) multiplexer_6 (
    .in0(registerfile_1_b_out), .in1(bit_extender_1_out), .out(multiplexer_6_out), .sel(controller_1_r_i));
  Controller controller_1 (
    .in_1(rom_1_data), .IMM8(controller_1_imm8), .REG_S(controller_1_reg_s),
    .SIGN_EXT(controller_1_sign_ext), .R_I(controller_1_r_i), .REG_D(controller_1_reg_d),
    .ALU_FUNC(controller_1_alu_func), .REG_WRITE(controller_1_reg_write), .MEM_WRITE(controller_1_mem_write),
    .JMP_MODE(controller_1_jmp_mode), .JMP(controller_1_jmp), .Written(controller_1_written));
  Multiplexer #(.width(16)) multiplexer_7 (
    .in0(registerfile_1_b_out), .in1(multiplexer_5_out), .out(multiplexer_7_out), .sel(controller_1_r_i));
  Multiplexer #(.select(2), .width(16)) multiplexer_8 (
    .in0(registerfile_1_b_out), .in1(multiplexer_5_out), .in2(ram_1_dout), .in3(main_1_out_5),
    .out(multiplexer_8_out), .sel(controller_1_written));
  main main_1 (
    .in_3(registerfile_1_a_out), .in_4(multiplexer_7_out), .in_2(controller_1_alu_func), .out_5(main_1_out_5));  // open: WRITE_FLAG
  RAM #(.addrWidth(16), .asyncread("true"), .dataWidth(16)) ram_1 (
    .addr(multiplexer_7_out), .we(controller_1_mem_write), .oe(1'b1), .clk(clock_2_out),
    .din(registerfile_1_a_out), .dout(ram_1_dout));
  Clock clock_2 (.out(clock_2_out));

  // Notes on the sheet:
  //   contents of rom_1 (hex, n*v repeats v):
  //   1805 190a d707 2007 8f01 2107 8f01 1a0a 2207 480b 7000 8f01 2307 1307 9b03 3003 8b01 3103 8b02 5823
  //   9801 8f01 2007 8f01 2107 8f01 1a1d 2207 480b 8801 1703 3307 9f01 3207 4002 1001 481e
endmodule

module Controller (
  input  [15:0] in_1,
  output [7:0] IMM8,
  output [2:0] REG_S,
  output SIGN_EXT,
  output R_I,
  output [2:0] REG_D,
  output [2:0] ALU_FUNC,
  output REG_WRITE,
  output MEM_WRITE,
  output [1:0] JMP_MODE,
  output JMP,
  output [1:0] Written
);

  wire and_1_out, nor_1_out, not_1_out, not_2_out, not_3_out, or_2_out, or_3_out, xor_1_out;

  or or_1 (Written[1], in_1[13], in_1[15]);
  Multiplexer multiplexer_1 (.in0(in_1[11]), .in1(in_1[15]), .out(Written[0]), .sel(Written[1]));
  and and_1 (and_1_out, Written[1], xor_1_out);
  or or_2 (or_2_out, and_1_out, MEM_WRITE);
  xor xor_1 (xor_1_out, Written[1], Written[0]);
  not not_1 (not_1_out, or_2_out);
  not not_2 (not_2_out, in_1[15]);
  or or_3 (or_3_out, in_1[15], in_1[12]);
  and and_2 (JMP, in_1[14], not_2_out);
  and and_3 (SIGN_EXT, in_1[7], not_1_out);
  nor nor_1 (nor_1_out, in_1[12], in_1[15], JMP);
  not not_3 (not_3_out, JMP);
  and and_4 (REG_WRITE, or_3_out, not_3_out);
  and and_5 (MEM_WRITE, nor_1_out, in_1[13]);

  assign ALU_FUNC = in_1[14:12];
  assign IMM8 = in_1[7:0];
  assign JMP_MODE = in_1[13:12];
  assign R_I = in_1[11];
  assign REG_D = in_1[10:8];
  assign REG_S = in_1[2:0];
endmodule

module IS_ZERO (
  input  [15:0] in_1,
  output out_2
);

  wire or_1_out, or_2_out, or_3_out, or_4_out, or_5_out, or_6_out, or_7_out, or_8_out, or_9_out, or_10_out,
       or_11_out, or_12_out, or_13_out, or_14_out, or_15_out;

  or or_1 (or_1_out, in_1[0], in_1[1]);
  or or_2 (or_2_out, in_1[2], in_1[3]);
  or or_3 (or_3_out, in_1[14], in_1[15]);
  or or_4 (or_4_out, in_1[12], in_1[13]);
  or or_5 (or_5_out, in_1[4], in_1[5]);
  or or_6 (or_6_out, in_1[8], in_1[9]);
  or or_7 (or_7_out, in_1[10], in_1[11]);
  or or_8 (or_8_out, in_1[6], in_1[7]);
  or or_9 (or_9_out, or_1_out, or_2_out);
  or or_10 (or_10_out, or_5_out, or_8_out);
  or or_11 (or_11_out, or_6_out, or_7_out);
  or or_12 (or_12_out, or_4_out, or_3_out);
  or or_13 (or_13_out, or_11_out, or_12_out);
  or or_14 (or_14_out, or_9_out, or_10_out);
  or or_15 (or_15_out, or_14_out, or_13_out);
  not not_1 (out_2, or_15_out);
endmodule

module Pipeline (
);

  wire clock_1_out, clock_2_out, controller_1_jmp, controller_1_mem_write, controller_1_r_i,
       controller_1_reg_write, controller_1_sign_ext, decode_register_1_ext, decode_register_1_jump,
       decode_register_1_mw, decode_register_1_r_or_i, decode_register_1_rw, exe_register_1_m_w,
       exe_register_1_r_w, jump_control_1_took, known_jumps_1_took, nor_1_out, not_1_out, not_2_out,
       not_3_out, s_r_ff_1_q, write_register_1_write_reg;
  wire [1:0] controller_1_jmp_mode, controller_1_written, decode_register_1_mode_jmp,
       decode_register_1_w_controll, exe_register_1_write_mode, write_register_1_w_controll;
  wire [2:0] controller_1_alu_func, controller_1_reg_d, controller_1_reg_s, decode_register_1_alu,
       decode_register_1_regd_out, decode_register_1_regs_out, exe_register_1_alu, exe_register_1_rd,
       write_register_1_reg_dest;
  wire [7:0] controller_1_imm8, decode_register_1_imm_out;
  wire [15:0] adder_1_out, bit_extender_1_out, bit_extender_2_out, decode_register_1_pc_out,
       exe_register_1_rd_out, exe_register_1_rs_out, forward_dest_1_val, forward_dest_2_val,
       jump_control_1_out_6, known_jumps_1_pc_upd, main_1_out_5, multiplexer_1_out, multiplexer_2_out,
       multiplexer_3_out, multiplexer_4_out, multiplexer_5_out, multiplexer_6_out, multiplexer_7_out,
       ram_1_dout, register_1_q, registerfile_1_a_out, registerfile_1_b_out, rom_1_data,
       write_register_1_alu_res, write_register_1_memory_res, write_register_1_rs_out;

  Register #(.width(16)) register_1 (
    .D(multiplexer_2_out), .en(1'b1), .Q(register_1_q), .clk(clock_1_out));  // open: clr
  ROM #(.addrWidth(16), .dataWidth(16)) rom_1 (.addr(register_1_q), .data(rom_1_data));
  Adder #(.width(16)) adder_1 (.a(register_1_q), .b(16'h1), .out(adder_1_out));  // open: cin, cout
  Clock clock_1 (.out(clock_1_out));
  Controller controller_1 (
    .in_1(rom_1_data), .IMM8(controller_1_imm8), .REG_S(controller_1_reg_s),
    .SIGN_EXT(controller_1_sign_ext), .R_I(controller_1_r_i), .REG_D(controller_1_reg_d),
    .ALU_FUNC(controller_1_alu_func), .REG_WRITE(controller_1_reg_write), .MEM_WRITE(controller_1_mem_write),
    .JMP_MODE(controller_1_jmp_mode), .JMP(controller_1_jmp), .Written(controller_1_written));
  S_R_Flip_Flop s_r_ff_1 (.S(not_2_out), .clk(clock_1_out), .R(nor_1_out), .Q(s_r_ff_1_q));  // open: Qn, preset, reset
  not not_1 (not_1_out, s_r_ff_1_q);
  not not_2 (not_2_out, nor_1_out);
  jump_control jump_control_1 (
    .JMP_MODE(decode_register_1_mode_jmp), .RS_IMM(multiplexer_3_out), .RD_VAL(forward_dest_1_val),
    .PC(decode_register_1_pc_out), .JMP(decode_register_1_jump), .out_6(jump_control_1_out_6),
    .TOOK(jump_control_1_took));
  nor nor_1 (nor_1_out, jump_control_1_took, known_jumps_1_took);
  Multiplexer #(.width(16)) multiplexer_1 (
    .in0(adder_1_out), .in1(known_jumps_1_pc_upd), .out(multiplexer_1_out), .sel(known_jumps_1_took));
  Multiplexer #(.width(16)) multiplexer_2 (
    .in0(multiplexer_1_out), .in1(jump_control_1_out_6), .out(multiplexer_2_out), .sel(jump_control_1_took));
  Multiplexer #(.width(16)) multiplexer_3 (
    .in0(bit_extender_1_out), .in1(forward_dest_2_val), .out(multiplexer_3_out), .sel(not_3_out));
  known_jumps known_jumps_1 (
    .R_I(controller_1_r_i), .JUMP_MODE(controller_1_jmp_mode), .IMM8(controller_1_imm8), .PC(register_1_q),
    .JMP(controller_1_jmp), .PC_UPD(known_jumps_1_pc_upd), .TOOK(known_jumps_1_took));
  Decode_register decode_register_1 (
    .IMM_8(controller_1_imm8), .REG_S(controller_1_reg_s), .SIGN_EXT(controller_1_sign_ext),
    .R_I(controller_1_r_i), .REG_D(controller_1_reg_d), .ALU_FUNC(controller_1_alu_func),
    .REG_WRITE(controller_1_reg_write), .MEM_WRITE(controller_1_mem_write), .JMP_MODE(controller_1_jmp_mode),
    .JMP(controller_1_jmp), .WRITTEN(controller_1_written), .PC(adder_1_out), .CLK(clock_1_out),
    .in_14(not_1_out), .IMM_OUT(decode_register_1_imm_out), .REGS_OUT(decode_register_1_regs_out),
    .EXT(decode_register_1_ext), .R_OR_I(decode_register_1_r_or_i), .REGD_OUT(decode_register_1_regd_out),
    .ALU(decode_register_1_alu), .RW(decode_register_1_rw), .MW(decode_register_1_mw),
    .MODE_JMP(decode_register_1_mode_jmp), .JUMP(decode_register_1_jump),
    .W_CONTROLL(decode_register_1_w_controll), .PC_OUT(decode_register_1_pc_out));
  not not_3 (not_3_out, decode_register_1_r_or_i);
  RegisterFile registerfile_1 (
    .RS(decode_register_1_regs_out), .WRITE_DATA(multiplexer_7_out), .WRITE_EN(write_register_1_write_reg),
    .REG_WRITE(write_register_1_reg_dest), .in_5(clock_1_out), .RD(decode_register_1_regd_out),
    .A_OUT(registerfile_1_a_out), .B_OUT(registerfile_1_b_out));
  assign bit_extender_1_out = {{8{1'b0}}, decode_register_1_imm_out};  // Bit_Extender bit_extender_1
  assign bit_extender_2_out = {{8{decode_register_1_imm_out[7]}}, decode_register_1_imm_out};  // Bit_Extender bit_extender_2
  Multiplexer #(.width(16)) multiplexer_4 (
    .in0(bit_extender_1_out), .in1(bit_extender_2_out), .out(multiplexer_4_out), .sel(decode_register_1_ext));
  FORWARD_DEST forward_dest_1 (
    .DECODE_REG(decode_register_1_regd_out), .DECODE_VAL(registerfile_1_a_out),
    .EXECUTE_REG(exe_register_1_rd), .EXECUTE_RW(exe_register_1_r_w),
    .EXECUTE_WRITTEN(exe_register_1_write_mode), .EXECUTE_ALU(main_1_out_5),
    .EXECUTE_RS_IMM8(exe_register_1_rs_out), .EXECUTE_MEM(ram_1_dout), .WRITE_REG(write_register_1_reg_dest),
    .WRITE_RW(write_register_1_write_reg), .WRITE_WRITTEN(write_register_1_w_controll),
    .WRITE_RS_IMM8(write_register_1_rs_out), .WRITE_MEM(write_register_1_memory_res),
    .WRITE_ALU(write_register_1_alu_res), .VAL(forward_dest_1_val));
  Multiplexer #(.width(16)) multiplexer_5 (
    .in0(registerfile_1_b_out), .in1(multiplexer_4_out), .out(multiplexer_5_out),
    .sel(decode_register_1_r_or_i));
  FORWARD_DEST forward_dest_2 (
    .DECODE_REG(decode_register_1_regs_out), .DECODE_VAL(multiplexer_5_out), .EXECUTE_REG(exe_register_1_rd),
    .EXECUTE_RW(exe_register_1_r_w), .EXECUTE_WRITTEN(exe_register_1_write_mode), .EXECUTE_ALU(main_1_out_5),
    .EXECUTE_RS_IMM8(exe_register_1_rs_out), .EXECUTE_MEM(ram_1_dout), .WRITE_REG(write_register_1_reg_dest),
    .WRITE_RW(write_register_1_write_reg), .WRITE_WRITTEN(write_register_1_w_controll),
    .WRITE_RS_IMM8(write_register_1_rs_out), .WRITE_MEM(write_register_1_memory_res),
    .WRITE_ALU(write_register_1_alu_res), .VAL(forward_dest_2_val));
  Multiplexer #(.width(16)) multiplexer_6 (
    .in0(forward_dest_2_val), .in1(multiplexer_5_out), .out(multiplexer_6_out), .sel(decode_register_1_r_or_i));
  Exe_register exe_register_1 (
    .ALU_FUNC(decode_register_1_alu), .REG_S(decode_register_1_regs_out), .REG_D(decode_register_1_regd_out),
    .RD_VAL(forward_dest_1_val), .RS_VAL(multiplexer_6_out), .WRITTEN(decode_register_1_w_controll),
    .REG_WRITE(decode_register_1_rw), .MEM_WRITE(decode_register_1_mw), .R_I(decode_register_1_ext),
    .JMP(decode_register_1_jump), .CLK(clock_1_out), .in_12(1'b1), .ALU(exe_register_1_alu),
    .RD(exe_register_1_rd), .RD_OUT(exe_register_1_rd_out), .RS_OUT(exe_register_1_rs_out),
    .WRITE_MODE(exe_register_1_write_mode), .R_W(exe_register_1_r_w), .M_W(exe_register_1_m_w));  // open: RS, R_OR_I, JUMP
  main main_1 (
    .in_3(exe_register_1_rd_out), .in_4(exe_register_1_rs_out), .in_2(exe_register_1_alu),
    .out_5(main_1_out_5));  // open: WRITE_FLAG
  Clock clock_2 (.out(clock_2_out));
  RAM #(.addrWidth(16), .asyncread("true"), .dataWidth(16)) ram_1 (
    .addr(exe_register_1_rs_out), .we(exe_register_1_m_w), .oe(1'b1), .clk(clock_2_out),
    .din(exe_register_1_rd_out), .dout(ram_1_dout));
  Multiplexer #(.select(2), .width(16)) multiplexer_7 (
    .in0(write_register_1_rs_out), .in1(write_register_1_rs_out), .in2(write_register_1_memory_res),
    .in3(write_register_1_alu_res), .out(multiplexer_7_out), .sel(write_register_1_w_controll));
  Write_register write_register_1 (
    .RD(exe_register_1_rd), .ALU_OP(main_1_out_5), .RS_VAL(exe_register_1_rs_out), .MEM_VAL(ram_1_dout),
    .WRITTEN(exe_register_1_write_mode), .W_REG(exe_register_1_r_w), .CLK(clock_2_out), .in_8(1'b1),
    .REG_DEST(write_register_1_reg_dest), .ALU_RES(write_register_1_alu_res),
    .RS_OUT(write_register_1_rs_out), .MEMORY_RES(write_register_1_memory_res),
    .W_CONTROLL(write_register_1_w_controll), .WRITE_REG(write_register_1_write_reg));

  // Notes on the sheet:
  //   contents of rom_1 (hex, n*v repeats v):
  //   d707 d101 1807 2007 8f01 1a08 2207 480a 2800 7000 8f01 2107 1107 8f01 2407 1301 9b02 3003 5829 9801
  //   5828 8f01 2007 8f01 1a1b 2207 480a 1400 1301 9b02 3003 8f01 9802 2007 8f01 1a26 2207 480a 8004 4829
  //   1801 1701 8f01 3407 9f01 3107 9f01 3207 4002
endmodule

module Decode_register (
  input  [7:0] IMM_8,
  input  [2:0] REG_S,
  input  SIGN_EXT,
  input  R_I,
  input  [2:0] REG_D,
  input  [2:0] ALU_FUNC,
  input  REG_WRITE,
  input  MEM_WRITE,
  input  [1:0] JMP_MODE,
  input  JMP,
  input  [1:0] WRITTEN,
  input  [15:0] PC,
  input  CLK,
  input  in_14,
  output [7:0] IMM_OUT,
  output [2:0] REGS_OUT,
  output EXT,
  output R_OR_I,
  output [2:0] REGD_OUT,
  output [2:0] ALU,
  output RW,
  output MW,
  output [1:0] MODE_JMP,
  output JUMP,
  output [1:0] W_CONTROLL,
  output [15:0] PC_OUT
);

  wire not_1_out, register_3_q, register_4_q, register_7_q, register_8_q, register_10_q, undriven;
  wire [1:0] register_9_q, register_11_q;
  wire [2:0] register_2_q, register_5_q, register_6_q;
  wire [7:0] register_1_q;
  wire [15:0] register_12_q;

  Register register_1 (.D(IMM_8), .en(1'b1), .Q(register_1_q), .clk(CLK), .clr(undriven));
  Register #(.width(3)) register_2 (.D(REG_S), .en(1'b1), .Q(register_2_q), .clk(CLK));  // open: clr
  Register #(.width(1)) register_3 (.D(SIGN_EXT), .en(1'b1), .Q(register_3_q), .clk(CLK));  // open: clr
  Register #(.width(1)) register_4 (.D(R_I), .en(1'b1), .Q(register_4_q), .clk(CLK));  // open: clr
  Register #(.width(3)) register_5 (.D(REG_D), .en(1'b1), .Q(register_5_q), .clk(CLK));  // open: clr
  Register #(.width(3)) register_6 (.D(ALU_FUNC), .en(1'b1), .Q(register_6_q), .clk(CLK));  // open: clr
  Register #(.width(1)) register_7 (.D(REG_WRITE), .en(1'b1), .Q(register_7_q), .clk(CLK));  // open: clr
  Register #(.width(1)) register_8 (.D(MEM_WRITE), .en(1'b1), .Q(register_8_q), .clk(CLK));  // open: clr
  Register #(.width(2)) register_9 (.D(JMP_MODE), .en(1'b1), .Q(register_9_q), .clk(CLK));  // open: clr
  Register #(.width(1)) register_10 (.D(JMP), .en(1'b1), .Q(register_10_q), .clk(CLK));  // open: clr
  Register #(.width(2)) register_11 (.D(WRITTEN), .en(1'b1), .Q(register_11_q), .clk(CLK));  // open: clr
  Register #(.width(16)) register_12 (.D(PC), .en(1'b1), .Q(register_12_q), .clk(CLK));  // open: clr
  not not_1 (not_1_out, in_14);
  Multiplexer #(.width(16)) multiplexer_1 (.in0(register_12_q), .in1({16{1'b0}}), .out(PC_OUT), .sel(not_1_out));
  Multiplexer #(.width(8)) multiplexer_2 (.in0(register_1_q), .in1({8{1'b0}}), .out(IMM_OUT), .sel(not_1_out));
  Multiplexer #(.width(3)) multiplexer_3 (.in0(register_2_q), .in1(3'b000), .out(REGS_OUT), .sel(not_1_out));
  Multiplexer multiplexer_4 (.in0(register_3_q), .in1(1'b0), .out(EXT), .sel(not_1_out));
  Multiplexer multiplexer_5 (.in0(register_4_q), .in1(1'b0), .out(R_OR_I), .sel(not_1_out));
  Multiplexer #(.width(3)) multiplexer_6 (.in0(register_5_q), .in1(3'b000), .out(REGD_OUT), .sel(not_1_out));
  Multiplexer #(.width(3)) multiplexer_7 (.in0(register_6_q), .in1(3'b000), .out(ALU), .sel(not_1_out));
  Multiplexer multiplexer_8 (.in0(register_7_q), .in1(1'b0), .out(RW), .sel(not_1_out));
  Multiplexer multiplexer_9 (.in0(register_8_q), .in1(1'b0), .out(MW), .sel(not_1_out));
  Multiplexer #(.width(2)) multiplexer_10 (.in0(register_9_q), .in1(2'b00), .out(MODE_JMP), .sel(not_1_out));
  Multiplexer multiplexer_11 (.in0(register_10_q), .in1(1'b0), .out(JUMP), .sel(not_1_out));
  Multiplexer #(.width(2)) multiplexer_12 (.in0(register_11_q), .in1(2'b00), .out(W_CONTROLL), .sel(not_1_out));
endmodule

module Exe_register (
  input  [2:0] ALU_FUNC,
  input  [2:0] REG_S,
  input  [2:0] REG_D,
  input  [15:0] RD_VAL,
  input  [15:0] RS_VAL,
  input  [1:0] WRITTEN,
  input  REG_WRITE,
  input  MEM_WRITE,
  input  R_I,
  input  JMP,
  input  CLK,
  input  in_12,
  output [2:0] ALU,
  output [2:0] RS,
  output [2:0] RD,
  output [15:0] RD_OUT,
  output [15:0] RS_OUT,
  output [1:0] WRITE_MODE,
  output R_W,
  output M_W,
  output R_OR_I,
  output JUMP
);

  Register #(.width(3)) register_1 (.D(ALU_FUNC), .en(in_12), .Q(ALU), .clk(CLK));  // open: clr
  Register #(.width(3)) register_2 (.D(REG_S), .en(in_12), .Q(RS), .clk(CLK));  // open: clr
  Register #(.width(3)) register_3 (.D(REG_D), .en(in_12), .Q(RD), .clk(CLK));  // open: clr
  Register #(.width(16)) register_4 (.D(RD_VAL), .en(in_12), .Q(RD_OUT), .clk(CLK));  // open: clr
  Register #(.width(16)) register_5 (.D(RS_VAL), .en(in_12), .Q(RS_OUT), .clk(CLK));  // open: clr
  Register #(.width(2)) register_6 (.D(WRITTEN), .en(in_12), .Q(WRITE_MODE), .clk(CLK));  // open: clr
  Register #(.width(1)) register_7 (.D(REG_WRITE), .en(in_12), .Q(R_W), .clk(CLK));  // open: clr
  Register #(.width(1)) register_8 (.D(MEM_WRITE), .en(in_12), .Q(M_W), .clk(CLK));  // open: clr
  Register #(.width(1)) register_9 (.D(R_I), .en(in_12), .Q(R_OR_I), .clk(CLK));  // open: clr
  Register #(.width(1)) register_10 (.D(JMP), .en(in_12), .Q(JUMP), .clk(CLK));  // open: clr
endmodule

module Mem_register (
  input  [15:0] RD_OUT,
  input  MEM_WRITE,
  input  REG_WRITE,
  input  [15:0] RS_OUT,
  input  [2:0] REG_D,
  input  [1:0] WRITTEN,
  input  [15:0] ALU,
  input  CLK,
  input  in_9,
  output [15:0] DATA,
  output M_W,
  output R_W,
  output [15:0] ADDR,
  output [2:0] RD,
  output [1:0] W_CONTROLL,
  output [15:0] ALU_R
);

  Register #(.width(16)) register_1 (.D(RD_OUT), .en(in_9), .Q(DATA), .clk(CLK));  // open: clr
  Register #(.width(1)) register_2 (.D(MEM_WRITE), .en(in_9), .Q(M_W), .clk(CLK));  // open: clr
  Register #(.width(1)) register_3 (.D(REG_WRITE), .en(in_9), .Q(R_W), .clk(CLK));  // open: clr
  Register #(.width(16)) register_4 (.D(RS_OUT), .en(in_9), .Q(ADDR), .clk(CLK));  // open: clr
  Register #(.width(3)) register_5 (.D(REG_D), .en(in_9), .Q(RD), .clk(CLK));  // open: clr
  Register #(.width(2)) register_6 (.D(WRITTEN), .en(in_9), .Q(W_CONTROLL), .clk(CLK));  // open: clr
  Register #(.width(16)) register_7 (.D(ALU), .en(in_9), .Q(ALU_R), .clk(CLK));  // open: clr
endmodule

module Write_register (
  input  [2:0] RD,
  input  [15:0] ALU_OP,
  input  [15:0] RS_VAL,
  input  [15:0] MEM_VAL,
  input  [1:0] WRITTEN,
  input  W_REG,
  input  CLK,
  input  in_8,
  output [2:0] REG_DEST,
  output [15:0] ALU_RES,
  output [15:0] RS_OUT,
  output [15:0] MEMORY_RES,
  output [1:0] W_CONTROLL,
  output WRITE_REG
);

  Register #(.width(3)) register_1 (.D(RD), .en(in_8), .Q(REG_DEST), .clk(CLK));  // open: clr
  Register #(.width(16)) register_2 (.D(ALU_OP), .en(in_8), .Q(ALU_RES), .clk(CLK));  // open: clr
  Register #(.width(16)) register_3 (.D(RS_VAL), .en(in_8), .Q(RS_OUT), .clk(CLK));  // open: clr
  Register #(.width(16)) register_4 (.D(MEM_VAL), .en(in_8), .Q(MEMORY_RES), .clk(CLK));  // open: clr
  Register #(.width(2)) register_5 (.D(WRITTEN), .en(in_8), .Q(W_CONTROLL), .clk(CLK));  // open: clr
  Register #(.width(1)) register_6 (.D(W_REG), .en(in_8), .Q(WRITE_REG), .clk(CLK));  // open: clr
endmodule

module FORWARD_DEST (
  input  [2:0] DECODE_REG,
  input  [15:0] DECODE_VAL,
  input  [2:0] EXECUTE_REG,
  input  EXECUTE_RW,
  input  [1:0] EXECUTE_WRITTEN,
  input  [15:0] EXECUTE_ALU,
  input  [15:0] EXECUTE_RS_IMM8,
  input  [15:0] EXECUTE_MEM,
  input  [2:0] WRITE_REG,
  input  WRITE_RW,
  input  [1:0] WRITE_WRITTEN,
  input  [15:0] WRITE_RS_IMM8,
  input  [15:0] WRITE_MEM,
  input  [15:0] WRITE_ALU,
  output [15:0] VAL
);

  wire not_1_out, not_2_out, not_3_out, or_1_out, or_2_out, or_3_out, or_4_out;
  wire [2:0] xor_1_out, xor_2_out;
  wire [15:0] multiplexer_1_out, multiplexer_2_out, multiplexer_3_out, multiplexer_4_out, multiplexer_5_out,
       multiplexer_6_out;

  Multiplexer #(.select(2), .width(16)) multiplexer_1 (
    .in0(EXECUTE_RS_IMM8), .in1(EXECUTE_RS_IMM8), .in2(EXECUTE_MEM), .in3(EXECUTE_ALU),
    .out(multiplexer_1_out), .sel(EXECUTE_WRITTEN));
  Multiplexer #(.select(2), .width(16)) multiplexer_2 (
    .in0(WRITE_RS_IMM8), .in1(WRITE_RS_IMM8), .in2(WRITE_MEM), .in3(WRITE_ALU), .out(multiplexer_2_out),
    .sel(WRITE_WRITTEN));
  Multiplexer #(.width(16)) multiplexer_3 (
    .in0(DECODE_VAL), .in1(multiplexer_1_out), .out(multiplexer_3_out), .sel(EXECUTE_RW));
  Multiplexer #(.width(16)) multiplexer_4 (
    .in0(DECODE_VAL), .in1(multiplexer_2_out), .out(multiplexer_4_out), .sel(WRITE_RW));
  assign xor_1_out = DECODE_REG ^ WRITE_REG;  // XOR_Gate xor_1, 3 bits wide
  assign xor_2_out = DECODE_REG ^ EXECUTE_REG;  // XOR_Gate xor_2, 3 bits wide
  or or_1 (or_1_out, xor_1_out[0], xor_1_out[1]);
  or or_2 (or_2_out, or_1_out, xor_1_out[2]);
  or or_3 (or_3_out, xor_2_out[0], xor_2_out[1]);
  Multiplexer #(.width(16)) multiplexer_5 (
    .in0(DECODE_VAL), .in1(multiplexer_4_out), .out(multiplexer_5_out), .sel(not_1_out));
  not not_1 (not_1_out, or_2_out);
  Multiplexer #(.width(16)) multiplexer_6 (
    .in0(DECODE_VAL), .in1(multiplexer_3_out), .out(multiplexer_6_out), .sel(not_2_out));
  not not_2 (not_2_out, or_4_out);
  or or_4 (or_4_out, or_3_out, xor_2_out[2]);
  not not_3 (not_3_out, not_2_out);
  Multiplexer #(.width(16)) multiplexer_7 (
    .in0(multiplexer_6_out), .in1(multiplexer_5_out), .out(VAL), .sel(not_3_out));
endmodule

module jump_control (
  input  [1:0] JMP_MODE,
  input  [15:0] RS_IMM,
  input  [15:0] RD_VAL,
  input  [15:0] PC,
  input  JMP,
  output [15:0] out_6,
  output TOOK
);

  wire is_zero_1_out_2, is_zero_2_out_2, not_1_out;
  wire [15:0] adder_1_out, multiplexer_1_out, multiplexer_2_out, multiplexer_3_out, subtractor_1_out;

  Adder #(.width(16)) adder_1 (.a(PC), .b(16'h1), .out(adder_1_out));  // open: cin, cout
  IS_ZERO is_zero_1 (.in_1(RD_VAL), .out_2(is_zero_1_out_2));
  Multiplexer #(.width(16)) multiplexer_1 (
    .in0(adder_1_out), .in1(RS_IMM), .out(multiplexer_1_out), .sel(is_zero_1_out_2));
  Multiplexer #(.width(16)) multiplexer_2 (
    .in0(RS_IMM), .in1(adder_1_out), .out(multiplexer_2_out), .sel(is_zero_1_out_2));
  Multiplexer #(.select(2), .width(16)) multiplexer_3 (
    .in0(RS_IMM), .in1(multiplexer_1_out), .in2(multiplexer_2_out), .in3(PC), .out(multiplexer_3_out),
    .sel(JMP_MODE));
  Multiplexer #(.width(16)) multiplexer_4 (.in0(multiplexer_3_out), .in1(adder_1_out), .out(out_6), .sel(not_1_out));
  not not_1 (not_1_out, JMP);
  Subtractor #(.width(16)) subtractor_1 (.a(out_6), .b(adder_1_out), .out(subtractor_1_out));  // open: bin, bout
  not not_2 (TOOK, is_zero_2_out_2);
  IS_ZERO is_zero_2 (.in_1(subtractor_1_out), .out_2(is_zero_2_out_2));
endmodule

module known_jumps (
  input  R_I,
  input  [1:0] JUMP_MODE,
  input  [7:0] IMM8,
  input  [15:0] PC,
  input  JMP,
  output [15:0] PC_UPD,
  output TOOK
);

  wire and_1_out, is_zero_1_out_2, not_1_out, xnor_1_out;
  wire [15:0] adder_1_out, bit_extender_1_out, multiplexer_1_out, multiplexer_2_out, multiplexer_3_out,
       subtractor_1_out;

  assign bit_extender_1_out = {{8{1'b0}}, IMM8};  // Bit_Extender bit_extender_1
  xnor xnor_1 (xnor_1_out, JUMP_MODE[0], JUMP_MODE[1]);
  Adder #(.width(16)) adder_1 (.a(16'h1), .b(PC), .out(adder_1_out));  // open: cin, cout
  Multiplexer #(.width(16)) multiplexer_1 (
    .in0(adder_1_out), .in1(bit_extender_1_out), .out(multiplexer_1_out), .sel(xnor_1_out));
  Multiplexer #(.width(16)) multiplexer_2 (
    .in0(adder_1_out), .in1(multiplexer_1_out), .out(multiplexer_2_out), .sel(R_I));
  and and_1 (and_1_out, JUMP_MODE[1], JUMP_MODE[0]);
  Multiplexer #(.width(16)) multiplexer_3 (.in0(multiplexer_2_out), .in1(PC), .out(multiplexer_3_out), .sel(and_1_out));
  not not_1 (not_1_out, JMP);
  Multiplexer #(.width(16)) multiplexer_4 (.in0(multiplexer_3_out), .in1(adder_1_out), .out(PC_UPD), .sel(not_1_out));
  Subtractor #(.width(16)) subtractor_1 (.a(PC_UPD), .b(adder_1_out), .out(subtractor_1_out));  // open: bin, bout
  IS_ZERO is_zero_1 (.in_1(subtractor_1_out), .out_2(is_zero_1_out_2));
  not not_2 (TOOK, is_zero_1_out_2);
endmodule
